# Fritzing sketch piddybot (saved by Fritzing 0.9.1b)
circuit board: 6.00002cm x 6.31cm
breadboards: 1

parts:
  P = POT [package=alps_pot]
  D = POT [package=alps_pot]
  M_2 = female pin header, 2 pins [form="♀ (female)"]
  M_1 = female pin header, 2 pins [form="♀ (female)"]
  I = POT [package=alps_pot]
  Nano = Arduino Nano (Rev3.0)
  Power = SPST Switch [package=switch-spdt_kit]
  Motors = SPST Switch [package=switch-spdt_kit]
  Battery = Generic female header - 3 pins [form="♀ (female)" package=THT]
  GY-85 = IMU Digital Combo Board 6DOF
  TB6612FNG = Motor Driver 1A Dual TB6612FNG
  JP5 = Header 1 [package=1x01_offset]  # not connected
  JP8 = Header 1 [package=1x01_offset]  # not connected
  JP9 = Header 1 [package=1x01_offset]  # not connected
  JP10 = Header 1 [package=1x01_offset]  # not connected
  JP11 = Header 1 [package=1x01_offset]  # not connected
  JP12 = Header 1 [package=1x01_offset]  # not connected
  JP13 = Header 1 [package=1x01_offset]  # not connected
  JP14 = Header 1 [package=1x01_offset]  # not connected
  JP15 = Header 1 [package=1x01_offset]  # not connected
  JP16 = Header 1 [package=1x01_offset]  # not connected
  JP17 = Header 1 [package=1x01_offset]  # not connected
  JP18 = Header 1 [package=1x01_offset]  # not connected
  JP19 = Header 1 [package=1x01_offset]  # not connected
  JP20 = Header 1 [package=1x01_offset]  # not connected
  JP21 = Header 1 [package=1x01_offset]  # not connected
  JP22 = Header 1 [package=1x01_offset]  # not connected
  S1 = Momentary Switch [package=ksa_sealed_tac_switch]

nets:
  5V: P.E, D.E, I.E, Nano.5V, GY-85.5V, TB6612FNG.VCC
  N1: P.S, Nano.A0
  GND: P.A, D.A, I.A, Nano.GND, Battery.GND, GY-85.GND, TB6612FNG.GND, S1.3, S1.4
  N2: D.S, Nano.A2
  N3: M_2.pin1, TB6612FNG.B02
  N4: M_2.pin2, TB6612FNG.B01
  N5: M_1.pin1, TB6612FNG.A01
  N6: M_1.pin2, TB6612FNG.A02
  N7: I.S, Nano.A1
  N8: Nano.D2, S1.1, S1.2
  N9: Nano.D3, TB6612FNG.PWMA
  N10: Nano.D5, TB6612FNG.PWMB
  N11: Nano.D8, TB6612FNG.AIN2
  N12: Nano.D9, TB6612FNG.AIN1
  N13: Nano.D10, TB6612FNG.STBY
  N14: Nano.D11/MOSI, TB6612FNG.BIN1
  N15: Nano.D12/MISO, TB6612FNG.BIN2
  N16: Nano.VIN, Power.P
  N17: Nano.A5, GY-85.SCL
  N18: Nano.A4, GY-85.SDA
  N19: Power.S, Motors.S, Battery.12V
  N20: Motors.P, TB6612FNG.VM

notes:
  by EXCO

custom parts:
  Generic female header - 3 pins: Generic female header
  IMU Digital Combo Board 6DOF: This is a simple breakout for the ADXL345 accelerometer and the ITG-3200 gyro. With this board, you get a full 6 degrees of freedom. The sensors communicate over I2C and one INT output pin from each sensor is broken out. If you need a simple and tiny board that gives you 6 degrees of freedom, this would be a good choice.
